# Fritzing sketch Project_setup (saved by Fritzing 0.9.9b)

parts:
  U1 = ESP32S-HiLetgo [part_number=ESP32S-HiLetgo]
  8x8_LED_Modul_mit_MAX1 = 8x8 LED Modul mit MAX7219 [package=THT]
  Photoresistor = PHOTOCELL [package=photocell]
  R2 = Resistor [tolerance=±5% resistance=10k package="2010 [SMD]"]
  TTP223B1 = TTP223B Capacitive Touch Sensor Module
  DS18B20 = KY-001 Temperature Sensor Module [package="Breakout board"]

nets:
  N1: U1.3.3, U1.GPIO27, Photoresistor.P$1
  N2: U1.GPIO26, DS18B20.S
  GND: U1.GND, 8x8_LED_Modul_mit_MAX1.GND_Eingang, R2.Pin_0, TTP223B1.GND, DS18B20.-
  VIN: U1.VIN, 8x8_LED_Modul_mit_MAX1.VCC_Eingang, TTP223B1.VCC, DS18B20.Vin
  N3: U1.GPIO15, TTP223B1.SIG
  N4: U1.GPIO2, 8x8_LED_Modul_mit_MAX1.CLK_Eingang
  N5: U1.GPIO0, 8x8_LED_Modul_mit_MAX1.CS_Eingang
  N6: U1.GPIO4, 8x8_LED_Modul_mit_MAX1.DIN_Eingang
  N7: Photoresistor.P$2, R2.Pin_1

custom parts:
  ESP32S-HiLetgo: HiLetgo ESP-WROOM-32 ESP32 ESP-32S Development Board 2.4GHz Dual-Mode WiFi + Bluetooth Dual Cores Microcontroller The ESP32 integrated with Antenna switches, RF Balun, power amplifiers, low-noise amplifiers, filters, and management modules, and the entire solution occupies the least area of PCB. 2.4 GHz Wi-Fi plus Bluetooth dual-mode chip, with TSMC Ultra-low power consumption 40nm technology,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
  TTP223B Capacitive Touch Sensor Module: The TTP223B capacitive touch sensor module uses the TTP223B IC. The appropriate voltage is approximately 2 to 5.5 volts.
  KY-001 Temperature Sensor Module: Arduino Temperature Sensor Module Keyes KY-001, Allows ambient temperature measurement using digital serial bus (DS18B20)
